// Logisim project 2107013_ALU_For_CPU.circ as structural Verilog: 9 circuits, main circuit main
module main (
  input  Control0,
  input  Control1,
  input  Control2,
  input  [27:0] A,
  input  [27:0] B,
  output [27:0] Result,
  output Zero,
  output Negative,
  output Carry,
  output Overflow
);

  wire [27:0] multiplexer_1_out, multiplexer_2_out, multiplexer_3_out, n28_bit_adder_subtractor_1_result,
       n28_bit_and_1_result, n28_bit_not_1_result, n28_bit_or_1_result, n28_bit_xor_1_result;

  _28_bit_xor u_28_bit_xor_1 (.A(A), .B(B), .Result(n28_bit_xor_1_result));
  _28_bit_not u_28_bit_not_1 (.A(A), .Result(n28_bit_not_1_result));
  _28_bit_AND u_28_bit_and_1 (.A(A), .B(B), .Result(n28_bit_and_1_result));
  _28_bit_OR u_28_bit_or_1 (.A(A), .B(B), .Result(n28_bit_or_1_result));
  _28_bit_adder_subtractor u_28_bit_adder_subtractor_1 (
    .A(A), .B(B), .Control(Control0), .Result(n28_bit_adder_subtractor_1_result), .Carry(Carry),
    .Overflow(Overflow));
  Multiplexer #(.width(28), .enable("false")) multiplexer_1 (
    .in0(n28_bit_xor_1_result), .in1(n28_bit_not_1_result), .out(multiplexer_1_out), .sel(Control1));
  Multiplexer #(.width(28), .enable("false")) multiplexer_2 (
    .in0(n28_bit_and_1_result), .in1(n28_bit_or_1_result), .out(multiplexer_2_out), .sel(Control0));
  Multiplexer #(.width(28), .enable("false")) multiplexer_3 (
    .in0(multiplexer_2_out), .in1(n28_bit_adder_subtractor_1_result), .out(multiplexer_3_out), .sel(Control1));
  Multiplexer #(.width(28), .enable("false")) multiplexer_4 (
    .in0(multiplexer_3_out), .in1(multiplexer_1_out), .out(Result), .sel(Control2));
  IS_zero_or_negative is_zero_or_negative_1 (.A(Result), .Zero(Zero), .Negative(Negative));

  // Notes on the sheet:
  //   ROLL: 2107013
  //   c2 c1 c0  -  Task
  //   000 - AND
  //   001 - OR
  //   010 - ADD
  //   011 - SUB
  //   100 - XOR
  //   110 - Bitwise NOT (Acc)
endmodule

// AND
module _28_bit_AND (
  input  [27:0] A,
  input  [27:0] B,
  output [27:0] Result
);

  assign Result = A & B;  // AND_Gate and_1, 28 bits wide
endmodule

// OR
module _28_bit_OR (
  input  [27:0] A,
  input  [27:0] B,
  output [27:0] Result
);

  assign Result = A | B;  // OR_Gate or_1, 28 bits wide
endmodule

module _1_bit_full_adder (
  input  A,
  input  B,
  input  Cin,
  output S,
  output Cout
);

  wire and_1_out, and_2_out, xor_1_out;

  xor xor_1 (xor_1_out, A, B);
  and and_1 (and_1_out, xor_1_out, Cin);
  and and_2 (and_2_out, B, A);
  xor xor_2 (S, xor_1_out, Cin);
  or or_1 (Cout, and_1_out, and_2_out);
endmodule

module _28_bit_full_adder (
  input  Cin,
  input  [27:0] A,
  input  [27:0] B,
  output [27:0] Sum,
  output Cout,
  output Overflow
);

  wire and_1_out, and_2_out, n1_bit_full_adder_1_cout, n1_bit_full_adder_2_cout, n1_bit_full_adder_3_cout,
       n1_bit_full_adder_4_cout, n1_bit_full_adder_5_cout, n1_bit_full_adder_6_cout,
       n1_bit_full_adder_7_cout, n1_bit_full_adder_8_cout, n1_bit_full_adder_9_cout,
       n1_bit_full_adder_10_cout, n1_bit_full_adder_11_cout, n1_bit_full_adder_12_cout,
       n1_bit_full_adder_13_cout, n1_bit_full_adder_14_cout, n1_bit_full_adder_15_cout,
       n1_bit_full_adder_16_cout, n1_bit_full_adder_17_cout, n1_bit_full_adder_18_cout,
       n1_bit_full_adder_19_cout, n1_bit_full_adder_20_cout, n1_bit_full_adder_21_cout,
       n1_bit_full_adder_22_cout, n1_bit_full_adder_23_cout, n1_bit_full_adder_24_cout,
       n1_bit_full_adder_25_cout, n1_bit_full_adder_26_cout, n1_bit_full_adder_27_cout, not_1_out, not_2_out,
       not_3_out;

  not not_1 (not_1_out, B[27]);
  not not_2 (not_2_out, A[27]);
  _1_bit_full_adder u_1_bit_full_adder_1 (.A(A[0]), .B(B[0]), .Cin(Cin), .Cout(n1_bit_full_adder_1_cout), .S(Sum[0]));
  _1_bit_full_adder u_1_bit_full_adder_2 (
    .A(A[1]), .B(B[1]), .Cin(n1_bit_full_adder_1_cout), .Cout(n1_bit_full_adder_2_cout), .S(Sum[1]));
  _1_bit_full_adder u_1_bit_full_adder_3 (
    .A(A[2]), .B(B[2]), .Cin(n1_bit_full_adder_2_cout), .Cout(n1_bit_full_adder_3_cout), .S(Sum[2]));
  _1_bit_full_adder u_1_bit_full_adder_4 (
    .A(A[3]), .B(B[3]), .Cin(n1_bit_full_adder_3_cout), .Cout(n1_bit_full_adder_4_cout), .S(Sum[3]));
  _1_bit_full_adder u_1_bit_full_adder_5 (
    .A(A[4]), .B(B[4]), .Cin(n1_bit_full_adder_4_cout), .Cout(n1_bit_full_adder_5_cout), .S(Sum[4]));
  _1_bit_full_adder u_1_bit_full_adder_6 (
    .A(A[5]), .B(B[5]), .Cin(n1_bit_full_adder_5_cout), .Cout(n1_bit_full_adder_6_cout), .S(Sum[5]));
  _1_bit_full_adder u_1_bit_full_adder_7 (
    .A(A[6]), .B(B[6]), .Cin(n1_bit_full_adder_6_cout), .Cout(n1_bit_full_adder_7_cout), .S(Sum[6]));
  _1_bit_full_adder u_1_bit_full_adder_8 (
    .A(A[7]), .B(B[7]), .Cin(n1_bit_full_adder_7_cout), .Cout(n1_bit_full_adder_8_cout), .S(Sum[7]));
  _1_bit_full_adder u_1_bit_full_adder_9 (
    .A(A[8]), .B(B[8]), .Cin(n1_bit_full_adder_8_cout), .Cout(n1_bit_full_adder_9_cout), .S(Sum[8]));
  _1_bit_full_adder u_1_bit_full_adder_10 (
    .A(A[9]), .B(B[9]), .Cin(n1_bit_full_adder_9_cout), .Cout(n1_bit_full_adder_10_cout), .S(Sum[9]));
  _1_bit_full_adder u_1_bit_full_adder_11 (
    .A(A[10]), .B(B[10]), .Cin(n1_bit_full_adder_10_cout), .Cout(n1_bit_full_adder_11_cout), .S(Sum[10]));
  _1_bit_full_adder u_1_bit_full_adder_12 (
    .A(A[11]), .B(B[11]), .Cin(n1_bit_full_adder_11_cout), .Cout(n1_bit_full_adder_12_cout), .S(Sum[11]));
  _1_bit_full_adder u_1_bit_full_adder_13 (
    .A(A[12]), .B(B[12]), .Cin(n1_bit_full_adder_12_cout), .Cout(n1_bit_full_adder_13_cout), .S(Sum[12]));
  _1_bit_full_adder u_1_bit_full_adder_14 (
    .A(A[13]), .B(B[13]), .Cin(n1_bit_full_adder_13_cout), .Cout(n1_bit_full_adder_14_cout), .S(Sum[13]));
  _1_bit_full_adder u_1_bit_full_adder_15 (
    .A(A[14]), .B(B[14]), .Cin(n1_bit_full_adder_14_cout), .Cout(n1_bit_full_adder_15_cout), .S(Sum[14]));
  _1_bit_full_adder u_1_bit_full_adder_16 (
    .A(A[15]), .B(B[15]), .Cin(n1_bit_full_adder_15_cout), .Cout(n1_bit_full_adder_16_cout), .S(Sum[15]));
  _1_bit_full_adder u_1_bit_full_adder_17 (
    .A(A[16]), .B(B[16]), .Cin(n1_bit_full_adder_16_cout), .Cout(n1_bit_full_adder_17_cout), .S(Sum[16]));
  _1_bit_full_adder u_1_bit_full_adder_18 (
    .A(A[17]), .B(B[17]), .Cin(n1_bit_full_adder_17_cout), .Cout(n1_bit_full_adder_18_cout), .S(Sum[17]));
  _1_bit_full_adder u_1_bit_full_adder_19 (
    .A(A[18]), .B(B[18]), .Cin(n1_bit_full_adder_18_cout), .Cout(n1_bit_full_adder_19_cout), .S(Sum[18]));
  _1_bit_full_adder u_1_bit_full_adder_20 (
    .A(A[19]), .B(B[19]), .Cin(n1_bit_full_adder_19_cout), .Cout(n1_bit_full_adder_20_cout), .S(Sum[19]));
  _1_bit_full_adder u_1_bit_full_adder_21 (
    .A(A[20]), .B(B[20]), .Cin(n1_bit_full_adder_20_cout), .Cout(n1_bit_full_adder_21_cout), .S(Sum[20]));
  _1_bit_full_adder u_1_bit_full_adder_22 (
    .A(A[21]), .B(B[21]), .Cin(n1_bit_full_adder_21_cout), .Cout(n1_bit_full_adder_22_cout), .S(Sum[21]));
  _1_bit_full_adder u_1_bit_full_adder_23 (
    .A(A[22]), .B(B[22]), .Cin(n1_bit_full_adder_22_cout), .Cout(n1_bit_full_adder_23_cout), .S(Sum[22]));
  _1_bit_full_adder u_1_bit_full_adder_24 (
    .A(A[23]), .B(B[23]), .Cin(n1_bit_full_adder_23_cout), .Cout(n1_bit_full_adder_24_cout), .S(Sum[23]));
  _1_bit_full_adder u_1_bit_full_adder_25 (
    .A(A[24]), .B(B[24]), .Cin(n1_bit_full_adder_24_cout), .Cout(n1_bit_full_adder_25_cout), .S(Sum[24]));
  _1_bit_full_adder u_1_bit_full_adder_26 (
    .A(A[25]), .B(B[25]), .Cin(n1_bit_full_adder_25_cout), .Cout(n1_bit_full_adder_26_cout), .S(Sum[25]));
  _1_bit_full_adder u_1_bit_full_adder_27 (
    .A(A[26]), .B(B[26]), .Cin(n1_bit_full_adder_26_cout), .Cout(n1_bit_full_adder_27_cout), .S(Sum[26]));
  _1_bit_full_adder u_1_bit_full_adder_28 (
    .A(A[27]), .B(B[27]), .Cin(n1_bit_full_adder_27_cout), .Cout(Cout), .S(Sum[27]));
  not not_3 (not_3_out, Sum[27]);
  and and_1 (and_1_out, B[27], A[27], not_3_out);
  and and_2 (and_2_out, Sum[27], not_2_out, not_1_out);
  or or_1 (Overflow, and_1_out, and_2_out);
endmodule

module _28_bit_adder_subtractor (
  input  Control,
  input  [27:0] A,
  input  [27:0] B,
  output [27:0] Result,
  output Carry,
  output Overflow
);

  wire [27:0] bit_extender_1_out, xor_1_out;

  assign bit_extender_1_out = {{27{Control}}, Control};  // Bit_Extender bit_extender_1
  assign xor_1_out = bit_extender_1_out ^ B;  // XOR_Gate xor_1, 28 bits wide
  _28_bit_full_adder u_28_bit_full_adder_1 (
    .A(A), .B(xor_1_out), .Cin(Control), .Sum(Result), .Cout(Carry), .Overflow(Overflow));
endmodule

module IS_zero_or_negative (
  input  [27:0] A,
  output Zero,
  output Negative
);

  nor nor_1 (Zero, A[13], A[0], A[1], A[2], A[3], A[4], A[5], A[6], A[7], A[8], A[9], A[10], A[11], A[12], A[14], A[15], A[16], A[17], A[18], A[19], A[20], A[21], A[22], A[23], A[24], A[25], A[26], A[27]);

  assign Negative = A[27];
endmodule

// XOR
module _28_bit_xor (
  input  [27:0] A,
  input  [27:0] B,
  output [27:0] Result
);

  assign Result = A ^ B;  // XOR_Gate xor_1, 28 bits wide
endmodule

// NOT
module _28_bit_not (
  input  [27:0] A,
  output [27:0] Result
);

  assign Result = ~A;  // NOT_Gate not_1, 28 bits wide
endmodule
