// Logisim project 2107013_CPU.circ as structural Verilog: 3 circuits, main circuit main
module main (
  input  Reset
);

  wire clock_1_out, cpu_1_r, cpu_1_w;
  wire [7:0] cpu_1_address;
  wire [27:0] cpu_1_dataout, ram_1_data;

  Clock clock_1 (.out(clock_1_out));
  CPU cpu_1 (
    .Clk(clock_1_out), .Reset(Reset), .Address(cpu_1_address), .R(cpu_1_r), .W(cpu_1_w), .DataIn(ram_1_data),
    .DataOut(cpu_1_dataout));
  RAM #(.dataWidth(28), .bus("separate")) ram_1 (
    .addr(cpu_1_address), .din(cpu_1_dataout), .data(ram_1_data), .str(cpu_1_w), .clk(clock_1_out),
    .ld(cpu_1_r));  // open: sel, clr

  // Notes on the sheet:
  //   0 - AND
  //   1 - ADD
  //   2 - STO
  //   3 - OR
  //   4 - SUB
  //   5 - BUN
  //   6 - LDA
  //   7 - HLT
  //   ROLL: 2107013
  //   8-XOR
  //   9-NOT
  //   Instruction Format (28 bit)
  //   __________________________
  //   | Don't Care | Op-Code | Address |
  //   __________________________
  //   |    16 bits    |    4 bits    |     8 bits   |
  //   __________________________
  //   RAM: 2⁸ * 28 bits = 896 Bytes
endmodule

module CPU (
  input  Clk,
  input  Reset,
  input  [27:0] DataIn,
  output [7:0] Address,
  output R,
  output W,
  output [27:0] DataOut
);

  wire b1, c0, c1, c2, controlunit_1_c1, controlunit_1_c2, d1, d2, LdA, LdA_from_MBR, LoadAc, LoadB, LoadMAR;
  wire [7:0] counter_1_q, multiplexer_1_out;
  wire [27:0] Ac, AcIn, ALUout, multiplexer_3_out;

  Multiplexer #(.width(8), .enable("false")) multiplexer_1 (
    .in0(counter_1_q), .in1(DataOut[7:0]), .out(multiplexer_1_out), .sel(d2));
  Multiplexer #(.width(28), .enable("false")) multiplexer_2 (
    .in0(ALUout), .in1(DataOut), .out(AcIn), .sel(LdA_from_MBR));
  Counter counter_1 (
    .load(controlunit_1_c2), .D(DataOut[7:0]), .count(controlunit_1_c1), .Q(counter_1_q), .clk(Clk),
    .clr(Reset));  // open: carry
  Register MAR (.D(multiplexer_1_out), .en(LoadMAR), .Q(Address), .clk(Clk), .clr(Reset));
  Register #(.width(4)) IR (.D(DataOut[11:8]), .en(controlunit_1_c1), .clk(Clk), .clr(Reset));  // open: Q
  ControlUnit controlunit_1 (
    .IR(DataOut[11:8]), .Clk(Clk), .d1(d1), .c1(controlunit_1_c1), .R(R), .c2(controlunit_1_c2), .d2(d2),
    .b1(b1), .W(W), .LdAfrB(LdA_from_MBR), .Operation({c2, c0, c1}), .LoadAc(LdA), .Reset(Reset));  // open: b2, b3
  Multiplexer #(.width(28), .enable("false")) multiplexer_3 (.in0(DataIn), .in1(Ac), .out(multiplexer_3_out), .sel(b1));
  or or_1 (LoadMAR, d1, d2);
  Register #(.width(28)) MBR (.D(multiplexer_3_out), .en(LoadB), .Q(DataOut), .clk(Clk), .clr(Reset));
  Register #(.width(28)) u_Ac (.D(AcIn), .en(LoadAc), .Q(Ac), .clk(Clk), .clr(Reset));
  _2107013_ALU_For_CPU_main main_1 (
    .A(Ac), .B(DataOut), .Control0(c0), .Control1(c1), .Control2(c2), .Result(ALUout));  // open: Zero, Negative, Carry, Overflow
  or or_2 (LoadB, R, b1);
  or or_3 (LoadAc, LdA_from_MBR, LdA);

  // Other names for the same wires on the sheet: MBRout[27:0] = DataOut; clr = Reset
endmodule

// CU
module ControlUnit (
  input  [3:0] IR,
  input  Clk,
  input  Reset,
  output d1,
  output c1,
  output R,
  output c2,
  output d2,
  output [2:0] Operation,
  output b1,
  output W,
  output b2,
  output LoadAc,
  output b3,
  output LdAfrB
);

  wire and_1_out, decoder_1_out6, decoder_1_out7, decoder_1_out8, decoder_1_out9, decoder_1_out15, not_1_out,
       or_1_out;
  wire [5:0] counter_1_q;
  wire [6:0] rom_1_data;

  Counter #(.width(6), .max('h3f)) counter_1 (
    .load(rom_1_data[2]), .D({IR, 2'b11}), .count(rom_1_data[0]), .Q(counter_1_q), .clk(and_1_out),
    .clr(or_1_out));  // open: carry
  or or_1 (or_1_out, rom_1_data[1], Reset);
  and and_1 (and_1_out, Clk, not_1_out);
  ROM #(.addrWidth(6), .dataWidth(7)) rom_1 (.addr(counter_1_q), .data(rom_1_data));  // open: sel
  not not_1 (not_1_out, decoder_1_out15);
  Decoder #(.select(4), .enable("false")) decoder_1 (
    .out1(d1), .out2(c1), .out3(R), .out4(c2), .out5(d2), .out6(decoder_1_out6), .out7(decoder_1_out7),
    .out8(decoder_1_out8), .out9(decoder_1_out9), .out10(b1), .out11(W), .out12(b2), .out13(b3),
    .out14(LdAfrB), .out15(decoder_1_out15), .sel(rom_1_data[6:3]));  // open: out0
  or or_2 (LoadAc, decoder_1_out6, decoder_1_out7, b2, decoder_1_out8, decoder_1_out9, b3);
  Priority_Encoder priority_encoder_1 (
    .in0(decoder_1_out6), .in1(decoder_1_out7), .in2(decoder_1_out8), .in3(decoder_1_out9), .in4(b2),
    .in5(b3), .in6(1'b0), .in7(1'b0), .out(Operation));  // open: en_in, gs, en_out

  // Notes on the sheet:
  //   contents of rom_1 (hex, n*v repeats v):
  //   9 19 14 29 19 31 2 29 19 39 2 29 51 59 2 29 19 41 2 29 19 49 2 21 2 2 2 29 19 71 2 78 0 0 0 29 19 61
  //   2 69 2
  //   c2 c1 c0  -  Task
  //   000 - AND
  //   001 - OR
  //   010 - ADD
  //   011 - SUB
  //   100 - XOR
  //   c2 c0 c1
  //   110 - Bitwise NOT (Acc)
endmodule
